# Fritzing sketch ups-v0 (saved by Fritzing 0.9.1b)
breadboards: 1

parts:
  J1 = male pin header, 2 pins [form="♂ (male)"]  # not connected
  J3_-_5V_DC = female pin header, 2 pins [form="♀ (female)"]
  J1_-_48V_DC = male pin header, 2 pins [form="♂ (male)"]
  J2_-_12V_DC = female pin header, 2 pins [form="♀ (female)"]
  U1 = Voltage Regulator - Variable [package="TO220 [THT]"]
  D1 = Rectifier Diode [part_number=1N4007 package="300 mil [THT]"]
  D2 = Rectifier Diode [part_number=1N4007 package="300 mil [THT]"]  # not connected
  D3 = Rectifier Diode [part_number=1N4007 package="300 mil [THT]"]  # not connected
  D4 = Rectifier Diode [part_number=1N4007 package="300 mil [THT]"]
  D5 = Rectifier Diode [part_number=1N4001 package="300 mil [THT]"]
  D6 = Rectifier Diode [part_number=1N4001 package="300 mil [THT]"]
  IC_741 = IC, DIP package, 8 pins [chip_label=IC741]
  LED1 = LED - 5mm [color="Red (633nm)" package="5 mm [THT]"]  # not connected
  LED2 = LED - 5mm [color="Green (570nm)" package="5 mm [THT]"]
  R1 = Resistor [tolerance=±5% resistance=330 package=THT]
  R2 = Resistor [tolerance=±5% resistance=47k package=THT]

nets:
  N1: J3_-_5V_DC.pin2, J1_-_48V_DC.pin2, J2_-_12V_DC.pin2, D4.cathode, R2.Pin_0
  N2: J1_-_48V_DC.pin1, U1.IN
  N3: J2_-_12V_DC.pin1, D5.cathode
  N4: U1.ADJ, D1.anode
  N5: U1.OUT, D6.anode
  N6: IC_741.pin6, LED2.cathode, LED2.anode, R1.Pin_0
