# Fritzing sketch my cape (saved by Fritzing 0.9.2b)
perfboards: 1

parts:
  J5 = shrouded pin header, 10 pins [form="♂ (shrouded male)"]  # not connected
  IC1 = IC, DIP package, 4 pins [chip_label=IC]  # not connected
  IC2 = IC, DIP package, 4 pins [chip_label=IC]
  IC3 = IC, DIP package, 4 pins [chip_label=IC]  # not connected
  IC4 = IC, DIP package, 4 pins [chip_label=IC]  # not connected
  IC5 = IC, DIP package, 4 pins [chip_label=IC]
  IC6 = IC, DIP package, 4 pins [chip_label=IC]  # not connected
  IC7 = IC, DIP package, 4 pins [chip_label=IC]
  IC8 = IC, DIP package, 4 pins [chip_label=IC]  # not connected
  IC9 = IC, SIP package, 9 pins [chip_label=IC]
  IC10 = IC, SIP package, 9 pins [chip_label=IC]
  J7 = longpad pin header, 23 pins [form="long pad"]  # not connected
  J9 = longpad pin header, 23 pins [form="long pad"]  # not connected
  U1 = 74HC595 [package="DIP16 [THT]"]
  LED1 = LED - 3mm [color="Red (633nm)" package="3 mm [THT]"]
  LED2 = LED - 3mm [color="Red (633nm)" package="3 mm [THT]"]  # not connected
  LED3 = LED - 3mm [color="Red (633nm)" package="3 mm [THT]"]
  LED4 = LED - 3mm [color="Red (633nm)" package="3 mm [THT]"]
  LED5 = LED - 3mm [color="Red (633nm)" package="3 mm [THT]"]
  LED6 = LED - 3mm [color="Red (633nm)" package="3 mm [THT]"]
  LED7 = LED - 3mm [color="Red (633nm)" package="3 mm [THT]"]
  LED8 = LED - 3mm [color="Red (633nm)" package="3 mm [THT]"]
  LED9 = LED - 3mm [color="Red (633nm)" part_number=zzzzz package="3 mm [THT]"]
  J8 = longpad pin header, 23 pins [form="long pad"]  # not connected
  J6 = longpad pin header, 23 pins [form="long pad"]  # not connected
  J10 = shrouded pin header, 20 pins [form="♂ (shrouded male)"]  # not connected

nets:
  N1: IC2.pin3, LED3.anode
  N2: IC5.pin3, LED1.anode
  N3: IC7.pin3, LED4.anode
  N4: IC9.pin1, U1.Q0
  N5: IC9.pin2, U1.Q1
  N6: IC9.pin3, U1.Q2
  N7: IC9.pin4, U1.Q3
  N8: IC9.pin5, U1.Q4
  N9: IC9.pin6, U1.Q5
  N10: IC9.pin7, U1.Q6
  N11: IC9.pin8, U1.Q7
  N12: IC9.pin9, U1.GND
  N13: IC10.pin2, LED1.cathode
  N14: IC10.pin3, LED3.cathode
  N15: IC10.pin4, LED4.cathode
  N16: IC10.pin5, LED5.cathode
  N17: IC10.pin6, LED6.cathode
  N18: IC10.pin7, LED7.cathode
  N19: IC10.pin8, LED8.cathode
  N20: IC10.pin9, LED9.cathode
