# Fritzing sketch my cape (saved by Fritzing 0.9.2b)
perfboards: 1

parts:
  J1 = shrouded pin header, 46 pins [form="♂ (shrouded male)"]  # not connected
  J2 = shrouded pin header, 46 pins [form="♂ (shrouded male)"]
  J3 = shrouded pin header, 10 pins [form="♂ (shrouded male)"]  # not connected
  J4 = shrouded pin header, 10 pins [form="♂ (shrouded male)"]  # not connected
  J5 = shrouded pin header, 10 pins [form="♂ (shrouded male)"]  # not connected
  LED3 = LED - 3mm [color="Red (633nm)" package="3 mm [THT]"]  # not connected
  R1 = RPACK* [package=rpack-sip-pth-5]  # not connected
  IC1 = IC, DIP package, 4 pins [chip_label=IC]  # not connected
  IC2 = IC, DIP package, 4 pins [chip_label=IC]  # not connected
  IC3 = IC, DIP package, 4 pins [chip_label=IC]  # not connected
  IC4 = IC, DIP package, 4 pins [chip_label=IC]  # not connected
  IC5 = IC, DIP package, 4 pins [chip_label=IC]  # not connected
  IC6 = IC, DIP package, 4 pins [chip_label=IC]  # not connected
  IC7 = IC, DIP package, 4 pins [chip_label=IC]  # not connected
  IC8 = IC, DIP package, 4 pins [chip_label=IC]  # not connected
  LED4 = LED - 3mm [color="Red (633nm)" package="3 mm [THT]"]  # not connected
  LED5 = LED - 3mm [color="Red (633nm)" package="3 mm [THT]"]  # not connected
  LED6 = LED - 3mm [color="Red (633nm)" package="3 mm [THT]"]  # not connected
  LED7 = LED - 3mm [color="Red (633nm)" package="3 mm [THT]"]  # not connected
  LED8 = LED - 3mm [color="Red (633nm)" package="3 mm [THT]"]  # not connected
  LED9 = LED - 3mm [color="Red (633nm)" package="3 mm [THT]"]  # not connected
  LED10 = LED - 3mm [color="Red (633nm)" package="3 mm [THT]"]  # not connected
  LED11 = LED - 3mm [color="Red (633nm)" package="3 mm [THT]"]  # not connected
  IC9 = IC, SIP package, 9 pins [chip_label=IC]
  IC10 = IC, SIP package, 9 pins [chip_label=IC]

nets:
  N1: J2.pin1, IC9.pin1, IC10.pin1
